// Logisim project Jason.HunterALU.circ as structural Verilog: 12 circuits, main circuit main
module main (
  input  [7:0] A,
  input  [7:0] B,
  input  [2:0] in_3,
  output [7:0] Output,
  output [7:0] Flags
);

  wire and_1_out, and_2_out, C1, C2, clock_1_out, clock_2_out, N, n8_bit_comparator_1_zero, not_1_out,
       not_2_out, not_3_out, V1, V2, Z;
  wire [6:0] Y;
  wire [7:0] Flags_t, n8_bit_adder_1_sum, n8_bit_bitwise_and_1_y, n8_bit_bitwise_or_1_y,
       n8_bit_bitwize_not_1_y, n8_bit_eor_1_y, n8_bit_multiplier_1_prod, n8_bit_subtractor_1_diff;
  wire [7:7] not_4_out;

  _8_bit_Register u_8_bit_register_1 (.In({N, Y}), .Clk(clock_1_out), .Out(Output));
  Clock clock_1 (.out(clock_1_out));
  _8_bit_Register u_8_bit_register_2 (.In(Flags_t), .Clk(clock_2_out), .Out(Flags));
  Clock clock_2 (.out(clock_2_out));
  _8_bit_Bitwise_And u_8_bit_bitwise_and_1 (.A(A), .B(B), .Y(n8_bit_bitwise_and_1_y));
  _8_bit_Bitwise_Or u_8_bit_bitwise_or_1 (.A(A), .B(B), .Y(n8_bit_bitwise_or_1_y));
  _8_bit_EOR u_8_bit_eor_1 (.A(A), .B(B), .Y(n8_bit_eor_1_y));
  _8_bit_Bitwize_Not u_8_bit_bitwize_not_1 (.A(A), .Y(n8_bit_bitwize_not_1_y));
  _8_bit_Adder u_8_bit_adder_1 (.A(A), .B(B), .Sum(n8_bit_adder_1_sum), .Carry(C1));
  _8_bit_Subtractor u_8_bit_subtractor_1 (.A(A), .B(B), .Diff(n8_bit_subtractor_1_diff), .Carry(C2));
  _8_bit_Multiplier u_8_bit_multiplier_1 (.A(A), .B(B), .Prod(n8_bit_multiplier_1_prod), .Ovf(V2));
  _8_bit_Comparator u_8_bit_comparator_1 (.A(A), .B(B), .Zero(n8_bit_comparator_1_zero));
  not not_1 (not_1_out, N);
  not not_2 (not_2_out, A[7]);
  not not_3 (not_3_out, B[7]);
  not not_4 (not_4_out[7], n8_bit_comparator_1_zero);
  and and_1 (and_1_out, not_1_out, A[7], B[7]);
  and and_2 (and_2_out, N, not_2_out, not_3_out);
  _8_bit_8x1_Multiplexer u_8_bit_8x1_multiplexer_1 (
    .D0(n8_bit_bitwise_and_1_y), .D1(n8_bit_bitwise_or_1_y), .D2(n8_bit_eor_1_y),
    .D3(n8_bit_bitwize_not_1_y), .D4(n8_bit_adder_1_sum), .D5(n8_bit_subtractor_1_diff),
    .D6(n8_bit_multiplier_1_prod), .D7({8{not_4_out[7]}}), .Output({N, Y}), .in_9(in_3));
  or or_1 (V1, and_1_out, and_2_out);
  _8_bit_Comparator u_8_bit_comparator_2 (.A({N, Y}), .B({8{1'b0}}), .Zero(Z));
  _8_bit_8x1_Multiplexer u_8_bit_8x1_multiplexer_2 (
    .D0({8{1'b0}}), .D1({8{1'b0}}), .D2({8{1'b0}}), .D3({8{1'b0}}), .D4({4'b0000, V1, C1, Z, N}),
    .D5({4'b0000, V1, C2, Z, N}), .D6({4'b0000, V2, 1'b0, Z, N}), .D7({{6{1'b0}}, Z, 1'b0}),
    .Output(Flags_t), .in_9(in_3));

  // Other names for the same wires on the sheet: Y[7] = N; N1 = A[7]; N2 = B[7]; S[2:0] = in_3
endmodule

module _8_bit_Bitwise_And (
  input  [7:0] A,
  input  [7:0] B,
  output [7:0] Y
);

  and and_1 (Y[0], A[0], B[0]);
  and and_2 (Y[1], A[1], B[1]);
  and and_3 (Y[2], A[2], B[2]);
  and and_4 (Y[3], A[3], B[3]);
  and and_5 (Y[4], A[4], B[4]);
  and and_6 (Y[5], A[5], B[5]);
  and and_7 (Y[6], A[6], B[6]);
  and and_8 (Y[7], A[7], B[7]);

  // Other names for the same wires on the sheet: S[7:0] = Y
endmodule

module _8_bit_Bitwise_Or (
  input  [7:0] A,
  input  [7:0] B,
  output [7:0] Y
);

  or or_1 (Y[0], A[0], B[0]);
  or or_2 (Y[1], A[1], B[1]);
  or or_3 (Y[2], A[2], B[2]);
  or or_4 (Y[3], A[3], B[3]);
  or or_5 (Y[4], A[4], B[4]);
  or or_6 (Y[5], A[5], B[5]);
  or or_7 (Y[6], A[6], B[6]);
  or or_8 (Y[7], A[7], B[7]);

  // Other names for the same wires on the sheet: S[7:0] = Y
endmodule

module _8_bit_Bitwize_Not (
  input  [7:0] A,
  output [7:0] Y
);

  not not_1 (Y[0], A[0]);
  not not_2 (Y[1], A[1]);
  not not_3 (Y[2], A[2]);
  not not_4 (Y[3], A[3]);
  not not_5 (Y[4], A[4]);
  not not_6 (Y[5], A[5]);
  not not_7 (Y[6], A[6]);
  not not_8 (Y[7], A[7]);

  // Other names for the same wires on the sheet: S[7:0] = Y
endmodule

module _8_bit_EOR (
  input  [7:0] A,
  input  [7:0] B,
  output [7:0] Y
);

  xor xor_1 (Y[0], A[0], B[0]);
  xor xor_2 (Y[1], A[1], B[1]);
  xor xor_3 (Y[2], A[2], B[2]);
  xor xor_4 (Y[3], A[3], B[3]);
  xor xor_5 (Y[4], A[4], B[4]);
  xor xor_6 (Y[5], A[5], B[5]);
  xor xor_7 (Y[6], A[6], B[6]);
  xor xor_8 (Y[7], A[7], B[7]);

  // Other names for the same wires on the sheet: S[7:0] = Y
endmodule

module Full_Adder (
  input  A,
  input  B,
  input  C,
  output Sum,
  output Carry
);

  wire and_1_out, and_2_out, xor_1_out;

  xor xor_1 (xor_1_out, A, B);
  xor xor_2 (Sum, xor_1_out, C);
  and and_1 (and_1_out, xor_1_out, C);
  and and_2 (and_2_out, B, A);
  or or_1 (Carry, and_1_out, and_2_out);
endmodule

module _8_bit_Adder (
  input  [7:0] A,
  input  [7:0] B,
  output [7:0] Sum,
  output Carry
);

  wire full_adder_1_carry, full_adder_2_carry, full_adder_3_carry, full_adder_4_carry, full_adder_5_carry,
       full_adder_6_carry, full_adder_7_carry;

  Full_Adder full_adder_1 (.A(1'b0), .B(A[0]), .Sum(Sum[0]), .C(B[0]), .Carry(full_adder_1_carry));
  Full_Adder full_adder_2 (.A(full_adder_1_carry), .B(A[1]), .Sum(Sum[1]), .C(B[1]), .Carry(full_adder_2_carry));
  Full_Adder full_adder_3 (.A(full_adder_2_carry), .B(A[2]), .Sum(Sum[2]), .C(B[2]), .Carry(full_adder_3_carry));
  Full_Adder full_adder_4 (.A(full_adder_3_carry), .B(A[3]), .Sum(Sum[3]), .C(B[3]), .Carry(full_adder_4_carry));
  Full_Adder full_adder_5 (.A(full_adder_4_carry), .B(A[4]), .Sum(Sum[4]), .C(B[4]), .Carry(full_adder_5_carry));
  Full_Adder full_adder_6 (.A(full_adder_5_carry), .B(A[5]), .Sum(Sum[5]), .C(B[5]), .Carry(full_adder_6_carry));
  Full_Adder full_adder_7 (.A(full_adder_6_carry), .B(A[6]), .Sum(Sum[6]), .C(B[6]), .Carry(full_adder_7_carry));
  Full_Adder full_adder_8 (.A(full_adder_7_carry), .B(A[7]), .Sum(Sum[7]), .C(B[7]), .Carry(Carry));

  // Other names for the same wires on the sheet: S[7:0] = Sum
endmodule

module _8_bit_Subtractor (
  input  [7:0] A,
  input  [7:0] B,
  output [7:0] Diff,
  output Carry
);

  wire full_adder_1_carry, full_adder_2_carry, full_adder_3_carry, full_adder_4_carry, full_adder_5_carry,
       full_adder_6_carry, full_adder_7_carry, full_adder_8_carry, not_1_out, not_2_out, not_3_out,
       not_4_out, not_5_out, not_6_out, not_7_out, not_8_out;

  Full_Adder full_adder_1 (.A(1'b1), .B(A[0]), .Sum(Diff[0]), .C(not_1_out), .Carry(full_adder_1_carry));
  not not_1 (not_1_out, B[0]);
  Full_Adder full_adder_2 (.A(full_adder_1_carry), .B(A[1]), .Sum(Diff[1]), .C(not_2_out), .Carry(full_adder_2_carry));
  not not_2 (not_2_out, B[1]);
  Full_Adder full_adder_3 (.A(full_adder_2_carry), .B(A[2]), .Sum(Diff[2]), .C(not_3_out), .Carry(full_adder_3_carry));
  not not_3 (not_3_out, B[2]);
  Full_Adder full_adder_4 (.A(full_adder_3_carry), .B(A[3]), .Sum(Diff[3]), .C(not_4_out), .Carry(full_adder_4_carry));
  not not_4 (not_4_out, B[3]);
  Full_Adder full_adder_5 (.A(full_adder_4_carry), .B(A[4]), .Sum(Diff[4]), .C(not_5_out), .Carry(full_adder_5_carry));
  not not_5 (not_5_out, B[4]);
  Full_Adder full_adder_6 (.A(full_adder_5_carry), .B(A[5]), .Sum(Diff[5]), .C(not_6_out), .Carry(full_adder_6_carry));
  not not_6 (not_6_out, B[5]);
  Full_Adder full_adder_7 (.A(full_adder_6_carry), .B(A[6]), .Sum(Diff[6]), .C(not_7_out), .Carry(full_adder_7_carry));
  not not_7 (not_7_out, B[6]);
  Full_Adder full_adder_8 (.A(full_adder_7_carry), .B(A[7]), .Sum(Diff[7]), .C(not_8_out), .Carry(full_adder_8_carry));
  not not_8 (not_8_out, B[7]);
  not not_9 (Carry, full_adder_8_carry);

  // Other names for the same wires on the sheet: S[7:0] = Diff
endmodule

module _8_bit_Multiplier (
  input  [7:0] A,
  input  [7:0] B,
  output [7:0] Prod,
  output Ovf
);

  wire C1, C2, C3, C4, C5, C6, n8_bit_adder_9_carry, O1, or_1_out;
  wire [0:0] n8_bit_bitwise_and_8_y, xor_1_out;
  wire [1:0] n8_bit_bitwise_and_7_y, O2;
  wire [2:0] n8_bit_bitwise_and_6_y, O3;
  wire [3:0] n8_bit_bitwise_and_5_y, O4;
  wire [4:0] n8_bit_bitwise_and_4_y, O5;
  wire [5:0] n8_bit_bitwise_and_3_y, O6;
  wire [6:0] n8_bit_bitwise_and_2_y, O7;
  wire [7:0] n8_bit_adder_1_sum, n8_bit_adder_2_sum, n8_bit_adder_3_sum, n8_bit_adder_4_sum,
       n8_bit_adder_5_sum, n8_bit_adder_6_sum, n8_bit_adder_7_sum, n8_bit_adder_8_sum, n8_bit_adder_9_sum,
       n8_bit_bitwise_and_1_y, n8_bit_eor_1_y, n8_bit_eor_2_y, n8_bit_eor_3_y;

  _8_bit_EOR u_8_bit_eor_1 (.A(A), .B({8{A[7]}}), .Y(n8_bit_eor_1_y));
  _8_bit_EOR u_8_bit_eor_2 (.A(B), .B({8{B[7]}}), .Y(n8_bit_eor_2_y));
  _8_bit_Adder u_8_bit_adder_1 (.A(n8_bit_eor_1_y), .B({{7{1'b0}}, A[7]}), .Sum(n8_bit_adder_1_sum));  // open: Carry
  _8_bit_Adder u_8_bit_adder_2 (.A(n8_bit_eor_2_y), .B({{7{1'b0}}, B[7]}), .Sum(n8_bit_adder_2_sum));  // open: Carry
  _8_bit_Bitwise_And u_8_bit_bitwise_and_1 (
    .A(n8_bit_adder_1_sum), .B({8{n8_bit_adder_2_sum[0]}}), .Y(n8_bit_bitwise_and_1_y));
  _8_bit_Bitwise_And u_8_bit_bitwise_and_2 (
    .A(n8_bit_adder_1_sum), .B({8{n8_bit_adder_2_sum[1]}}), .Y({O1, n8_bit_bitwise_and_2_y}));
  _8_bit_Bitwise_And u_8_bit_bitwise_and_3 (
    .A(n8_bit_adder_1_sum), .B({8{n8_bit_adder_2_sum[2]}}), .Y({O2, n8_bit_bitwise_and_3_y}));
  _8_bit_Bitwise_And u_8_bit_bitwise_and_4 (
    .A(n8_bit_adder_1_sum), .B({8{n8_bit_adder_2_sum[3]}}), .Y({O3, n8_bit_bitwise_and_4_y}));
  _8_bit_Bitwise_And u_8_bit_bitwise_and_5 (
    .A(n8_bit_adder_1_sum), .B({8{n8_bit_adder_2_sum[4]}}), .Y({O4, n8_bit_bitwise_and_5_y}));
  _8_bit_Bitwise_And u_8_bit_bitwise_and_6 (
    .A(n8_bit_adder_1_sum), .B({8{n8_bit_adder_2_sum[5]}}), .Y({O5, n8_bit_bitwise_and_6_y}));
  _8_bit_Bitwise_And u_8_bit_bitwise_and_7 (
    .A(n8_bit_adder_1_sum), .B({8{n8_bit_adder_2_sum[6]}}), .Y({O6, n8_bit_bitwise_and_7_y}));
  _8_bit_Bitwise_And u_8_bit_bitwise_and_8 (
    .A(n8_bit_adder_1_sum), .B({8{n8_bit_adder_2_sum[7]}}), .Y({O7, n8_bit_bitwise_and_8_y[0]}));
  _8_bit_Adder u_8_bit_adder_3 (
    .A(n8_bit_bitwise_and_1_y), .B({n8_bit_bitwise_and_2_y, 1'b0}), .Sum(n8_bit_adder_3_sum), .Carry(C1));
  _8_bit_Adder u_8_bit_adder_4 (
    .A(n8_bit_adder_3_sum), .B({n8_bit_bitwise_and_3_y, 2'b00}), .Sum(n8_bit_adder_4_sum), .Carry(C2));
  _8_bit_Adder u_8_bit_adder_5 (
    .A(n8_bit_adder_4_sum), .B({n8_bit_bitwise_and_4_y, 3'b000}), .Sum(n8_bit_adder_5_sum), .Carry(C3));
  _8_bit_Adder u_8_bit_adder_6 (
    .A(n8_bit_adder_5_sum), .B({n8_bit_bitwise_and_5_y, 4'b0000}), .Sum(n8_bit_adder_6_sum), .Carry(C4));
  _8_bit_Adder u_8_bit_adder_7 (
    .A(n8_bit_adder_6_sum), .B({n8_bit_bitwise_and_6_y, {5{1'b0}}}), .Sum(n8_bit_adder_7_sum), .Carry(C5));
  _8_bit_Adder u_8_bit_adder_8 (
    .A(n8_bit_adder_7_sum), .B({n8_bit_bitwise_and_7_y, {6{1'b0}}}), .Sum(n8_bit_adder_8_sum), .Carry(C6));
  _8_bit_Adder u_8_bit_adder_9 (
    .A(n8_bit_adder_8_sum), .B({n8_bit_bitwise_and_8_y[0], {7{1'b0}}}), .Sum(n8_bit_adder_9_sum),
    .Carry(n8_bit_adder_9_carry));
  _8_bit_EOR u_8_bit_eor_3 (.A({8{xor_1_out[0]}}), .B(n8_bit_adder_9_sum), .Y(n8_bit_eor_3_y));
  xor xor_1 (xor_1_out[0], A[7], B[7]);
  _8_bit_Adder u_8_bit_adder_10 (.A(n8_bit_eor_3_y), .B({{7{1'b0}}, xor_1_out[0]}), .Sum(Prod));  // open: Carry
  or or_1 (or_1_out, n8_bit_adder_9_carry, C6, C5, C4, C3, C2, C1);
  or or_2 (Ovf, O1, O2[0], O2[1], O3[0], O3[1], O3[2], O4[0], O4[1], O4[2], O4[3], O5[0], O5[1], O5[2], O5[3], O5[4], n8_bit_adder_9_sum[7], O6[0], O6[1], O6[2], O6[3], O6[4], O6[5], O7[0], O7[1], O7[2], O7[3], O7[4], O7[5], O7[6], or_1_out);

  // Other names for the same wires on the sheet: SignA = A[7]; SignB = B[7]; P[7:0] = Prod
endmodule

module _8_bit_Comparator (
  input  [7:0] A,
  input  [7:0] B,
  output Zero
);

  wire or_1_out;
  wire [7:0] n8_bit_eor_1_y;

  _8_bit_EOR u_8_bit_eor_1 (.A(A), .B(B), .Y(n8_bit_eor_1_y));
  or or_1 (or_1_out, n8_bit_eor_1_y[0], n8_bit_eor_1_y[1], n8_bit_eor_1_y[2], n8_bit_eor_1_y[3], n8_bit_eor_1_y[4], n8_bit_eor_1_y[5], n8_bit_eor_1_y[6], n8_bit_eor_1_y[7]);
  not not_1 (Zero, or_1_out);
endmodule

module _8_bit_8x1_Multiplexer (
  input  [7:0] D0,
  input  [7:0] D1,
  input  [7:0] D2,
  input  [7:0] D3,
  input  [7:0] D4,
  input  [7:0] D5,
  input  [7:0] D6,
  input  [7:0] D7,
  input  [2:0] in_9,
  output [7:0] Output
);

  wire not_1_out, not_2_out, not_3_out, not_4_out, not_5_out, not_6_out, not_7_out, not_8_out, not_9_out,
       not_10_out, not_11_out, not_12_out;
  wire [7:0] n8_bit_bitwise_and_1_y, n8_bit_bitwise_and_2_y, n8_bit_bitwise_and_3_y, n8_bit_bitwise_and_4_y,
       n8_bit_bitwise_and_5_y, n8_bit_bitwise_and_6_y, n8_bit_bitwise_and_7_y, n8_bit_bitwise_and_8_y,
       n8_bit_bitwise_or_1_y, n8_bit_bitwise_or_2_y, n8_bit_bitwise_or_3_y, n8_bit_bitwise_or_4_y,
       n8_bit_bitwise_or_5_y, n8_bit_bitwise_or_6_y;
  wire [7:7] and_1_out, and_2_out, and_3_out, and_4_out, and_5_out, and_6_out, and_7_out, and_8_out;

  not not_1 (not_1_out, in_9[0]);
  not not_2 (not_2_out, in_9[1]);
  not not_3 (not_3_out, in_9[2]);
  not not_4 (not_4_out, in_9[1]);
  not not_5 (not_5_out, in_9[2]);
  not not_6 (not_6_out, in_9[0]);
  not not_7 (not_7_out, in_9[2]);
  not not_8 (not_8_out, in_9[2]);
  not not_9 (not_9_out, in_9[0]);
  not not_10 (not_10_out, in_9[1]);
  not not_11 (not_11_out, in_9[1]);
  not not_12 (not_12_out, in_9[0]);
  and and_1 (and_1_out[7], not_1_out, not_2_out, not_3_out);
  and and_2 (and_2_out[7], in_9[0], not_4_out, not_5_out);
  and and_3 (and_3_out[7], not_6_out, in_9[1], not_7_out);
  and and_4 (and_4_out[7], in_9[0], in_9[1], not_8_out);
  and and_5 (and_5_out[7], not_9_out, not_10_out, in_9[2]);
  and and_6 (and_6_out[7], in_9[0], not_11_out, in_9[2]);
  and and_7 (and_7_out[7], not_12_out, in_9[1], in_9[2]);
  and and_8 (and_8_out[7], in_9[0], in_9[1], in_9[2]);
  _8_bit_Bitwise_And u_8_bit_bitwise_and_1 (.A({8{and_1_out[7]}}), .B(D0), .Y(n8_bit_bitwise_and_1_y));
  _8_bit_Bitwise_And u_8_bit_bitwise_and_2 (.A({8{and_2_out[7]}}), .B(D1), .Y(n8_bit_bitwise_and_2_y));
  _8_bit_Bitwise_And u_8_bit_bitwise_and_3 (.A({8{and_3_out[7]}}), .B(D2), .Y(n8_bit_bitwise_and_3_y));
  _8_bit_Bitwise_And u_8_bit_bitwise_and_4 (.A({8{and_4_out[7]}}), .B(D3), .Y(n8_bit_bitwise_and_4_y));
  _8_bit_Bitwise_And u_8_bit_bitwise_and_5 (.A({8{and_5_out[7]}}), .B(D4), .Y(n8_bit_bitwise_and_5_y));
  _8_bit_Bitwise_And u_8_bit_bitwise_and_6 (.A({8{and_6_out[7]}}), .B(D5), .Y(n8_bit_bitwise_and_6_y));
  _8_bit_Bitwise_And u_8_bit_bitwise_and_7 (.A({8{and_7_out[7]}}), .B(D6), .Y(n8_bit_bitwise_and_7_y));
  _8_bit_Bitwise_And u_8_bit_bitwise_and_8 (.A({8{and_8_out[7]}}), .B(D7), .Y(n8_bit_bitwise_and_8_y));
  _8_bit_Bitwise_Or u_8_bit_bitwise_or_1 (
    .A(n8_bit_bitwise_and_1_y), .B(n8_bit_bitwise_and_2_y), .Y(n8_bit_bitwise_or_1_y));
  _8_bit_Bitwise_Or u_8_bit_bitwise_or_2 (
    .A(n8_bit_bitwise_and_3_y), .B(n8_bit_bitwise_and_4_y), .Y(n8_bit_bitwise_or_2_y));
  _8_bit_Bitwise_Or u_8_bit_bitwise_or_3 (
    .A(n8_bit_bitwise_and_5_y), .B(n8_bit_bitwise_and_6_y), .Y(n8_bit_bitwise_or_3_y));
  _8_bit_Bitwise_Or u_8_bit_bitwise_or_4 (
    .A(n8_bit_bitwise_and_7_y), .B(n8_bit_bitwise_and_8_y), .Y(n8_bit_bitwise_or_4_y));
  _8_bit_Bitwise_Or u_8_bit_bitwise_or_5 (
    .A(n8_bit_bitwise_or_1_y), .B(n8_bit_bitwise_or_2_y), .Y(n8_bit_bitwise_or_5_y));
  _8_bit_Bitwise_Or u_8_bit_bitwise_or_6 (
    .A(n8_bit_bitwise_or_3_y), .B(n8_bit_bitwise_or_4_y), .Y(n8_bit_bitwise_or_6_y));
  _8_bit_Bitwise_Or u_8_bit_bitwise_or_7 (.A(n8_bit_bitwise_or_5_y), .B(n8_bit_bitwise_or_6_y), .Y(Output));
endmodule

module _8_bit_Register (
  input  [7:0] In,
  input  Clk,
  output [7:0] Out
);

  D_Flip_Flop d_ff_1 (.clk(Clk), .D(In[0]), .Q(Out[0]));  // open: Qn, preset, en, reset
  D_Flip_Flop d_ff_2 (.clk(Clk), .D(In[1]), .Q(Out[1]));  // open: Qn, preset, en, reset
  D_Flip_Flop d_ff_3 (.clk(Clk), .D(In[2]), .Q(Out[2]));  // open: Qn, preset, en, reset
  D_Flip_Flop d_ff_4 (.clk(Clk), .D(In[3]), .Q(Out[3]));  // open: Qn, preset, en, reset
  D_Flip_Flop d_ff_5 (.clk(Clk), .D(In[4]), .Q(Out[4]));  // open: Qn, preset, en, reset
  D_Flip_Flop d_ff_6 (.clk(Clk), .D(In[5]), .Q(Out[5]));  // open: Qn, preset, en, reset
  D_Flip_Flop d_ff_7 (.clk(Clk), .D(In[6]), .Q(Out[6]));  // open: Qn, preset, en, reset
  D_Flip_Flop d_ff_8 (.clk(Clk), .D(In[7]), .Q(Out[7]));  // open: Qn, preset, en, reset
endmodule
